# Fritzing sketch bike_85 (saved by Fritzing 0.9.3b)
circuit board: 8.46667cm x 5.64444cm
breadboards: 1

parts:
  7219 = MAX7219 [package=dil24]
  ATTINY85 = ATTINY45 [package=so]
  U1 = 7-SEGMENT-4DIGIT [package=7-segment-4digit-youngsun]
  U2 = HALL-EFFECT [package=sc70]
  IC1 = Voltage Regulator [package=to220-igo]
  VCC = Battery block 9V

nets:
  N1: 7219.DIN, ATTINY85.PB0(MOSI)
  N2: 7219.DIG0, U1.7
  GND: 7219.GND, 7219.GND2, ATTINY85.GND, U2.GND, IC1.GND, VCC.-
  N3: 7219.DIG2, U1.13
  N4: 7219.DIG3, U1.6
  N5: 7219.DIG1, U1.11
  N6: 7219.LOAD, ATTINY85.PB2(SCK_ADC1)
  N7: 7219.CLK, ATTINY85.PB1(MISO)
  N8: 7219.SEGA, U1.8
  N9: 7219.SEGF, U1.9
  N10: 7219.SEGB, U1.14
  N11: 7219.SEGG, U1.5
  N12: 7219.SEGC, U1.4
  N13: 7219.SEGE, U1.1
  N14: 7219.SEGDP, U1.3
  N15: 7219.SEGD, U1.2
  N16: ATTINY85.PB4(ADC2), U2.OUT
  N17: ATTINY85.VCC, IC1.OUT
  N18: IC1.IN, VCC.+
